# Fritzing sketch schalter (saved by Fritzing 0.9.3b)
circuit board: 8.46667cm x 5.64444cm
breadboards: 1

parts:
  U1 = 74HC595 [part_number=SN74LS165]
  U2 = 74HC595 [part_number=SN74LS165]
  U3 = 74HC595 [part_number=SN74LS165]
  Bauteil1 = Arduino Leonardo (Rev3b)

nets:
  N1: U1.connector0, U2.connector0, U3.connector0
  N2: U1.connector7, U1.connector14, U2.connector7, U2.connector14, U3.connector7, U3.connector14
  N3: U1.connector9, U2.connector8, Bauteil1.D4/A6
  N4: U1.connector15, U2.connector15, U3.connector15
  N5: U2.connector1, U3.connector1
  N6: U2.connector9, U3.connector8
